# Fritzing sketch pedalproto1 (saved by Fritzing 0.9.10b)
circuit board: 14.7518cm x 6.33387cm
breadboards: 2

parts:
  U1 = POT [knob_status=50% power=0.5W package=pot_alpha_rv16af-20]
  S1 = Round Pushbutton
  ADC1 = MCP3008 [package=dil16]
  S2 = Round Pushbutton
  S3 = Round Pushbutton
  S4 = Round Pushbutton
  S5 = Round Pushbutton
  S8 = Round Pushbutton
  S7 = Round Pushbutton
  S6 = Round Pushbutton
  U2 = POT [knob_status=50% power=0.5W package=pot_alpha_rv16af-20]
  U3 = POT [knob_status=50% power=0.5W package=pot_alpha_rv16af-20]
  U4 = POT [knob_status=50% power=0.5W package=pot_alpha_rv16af-20]
  U5 = POT [knob_status=50% power=0.5W package=pot_alpha_rv16af-20]
  U6 = POT [knob_status=50% power=0.5W package=pot_alpha_rv16af-20]
  U7 = POT [knob_status=50% power=0.5W package=pot_alpha_rv16af-20]
  U8 = POT [knob_status=50% power=0.5W package=pot_alpha_rv16af-20]
  Pro_Micro = Arduino Pro Mini v13

nets:
  N1: U1.A, S1.leg1, ADC1.DGND, ADC1.AGND, S2.leg1, S3.leg1, S4.leg1, S5.leg1, S8.leg1, S7.leg1, S6.leg1, U2.A, U3.A, U4.A, U5.A, U6.A, U7.A, U8.A, Pro_Micro.GND
  N2: U1.S, ADC1.CH0
  VDD: U1.E, ADC1.VREF, ADC1.VDD, U2.E, U3.E, U4.E, U5.E, U6.E, U7.E, U8.E, Pro_Micro.VCC
  N3: S1.leg0, Pro_Micro.D9_PWM
  N4: ADC1.CH1, U2.S
  N5: ADC1.CH2, U3.S
  N6: ADC1.CH3, U4.S
  N7: ADC1.CH4, U5.S
  N8: ADC1.CH5, U6.S
  N9: ADC1.CH6, U7.S
  N10: ADC1.CH7, U8.S
  N11: ADC1.CS/SHDN, Pro_Micro.D10_PWM/SS
  N12: ADC1.Din, Pro_Micro.D11_PWM/MOSI
  N13: ADC1.Dout, Pro_Micro.D12/MISO
  N14: ADC1.CLK, Pro_Micro.D13/SCK
  N15: S2.leg0, Pro_Micro.D8
  N16: S3.leg0, Pro_Micro.D7
  N17: S4.leg0, Pro_Micro.D6_PWM
  N18: S5.leg0, Pro_Micro.D5_PWM
  N19: S8.leg0, Pro_Micro.D2
  N20: S7.leg0, Pro_Micro.D3_PWM
  N21: S6.leg0, Pro_Micro.D4

// code stored in the sketch: midibasspedal.ino

#include "MIDIUSB.h"
#include "MCP_ADC.h"

//Declare ADC
MCP3008 adc;

//Number of pots connected to ADC
const int potsQty = 8;

//Pots midi controller number
const int potsMidiController[potsQty] = { 16, 17, 18, 19 , 20 , 21 , 22 , 23};

//Pots previous values
int potsPrevVal[potsQty];

//Quanty of buttons connected to digital IO
const int buttonsQty = 8;

//Buttons pin definitions
const int buttonsPin[buttonsQty] = { 9, 8, 7, 6, 5, 4, 3, 2 };
//Buttons midi controller numner
const int buttonsMidiController[buttonsQty] = { 8, 9, 10, 11, 12, 13, 14, 15 };
//ADC chip select pin
const int ADC_CSPin = 10;

//Midi channel to operate on
const byte midiChannel = 0;

void setup() {
  Serial.begin(115200);

  adc.begin(ADC_CSPin);

  //Set all pins to input
  for (int button = 0; button < buttonsQty; button++) {
    pinMode(buttonsPin[button], INPUT_PULLUP);
  }
  //Gather all pots initial values
  for (int port = 0; port < potsQty; port++) {
    potsPrevVal[port] = mapPot(adc.analogRead(port));
  }
}

//Map ADC reading to midi value 0-127
int mapPot(int value) {
  return int(map(value, 0, 1023, 0, 127));
}

//Send midi control change
void controlChange(byte channel, byte control, byte value) {
  midiEventPacket_t event = { (byte)0x0B, (byte)0xB0 | channel, control, value };
  MidiUSB.sendMIDI(event);
  MidiUSB.flush();
}

//Receive guitariX preset change
// void midiPresetReturn() {
//   midiEventPacket_t rx;
//   bool receivedPacket = false;
//   do {
//     rx = MidiUSB.read();
//     switch (rx.header) {
//       case 0xC:
//         Serial.print("Preset Changed to:");
//         Serial.println(rx.byte2);
//         break;
//     }
//   } while (rx.header != 0);
// }

void loop() {
  //Read buttons input and send to midi accordingly
  for (int button = 0; button < buttonsQty; button++) {
    if (digitalRead(buttonsPin[button]) == LOW) {
      controlChange(midiChannel, buttonsMidiController[button], 127);
      //delay(250);
      // Serial.print("Switch # ");
      // Serial.print(button);
      // Serial.println(" pressed");
      continue;
    }
  }

  int tmpRead = 0;  //temporary reading of pots to send midi only on change

  //Read all pots values and send to midi accordingly
  for (int port = 0; port < potsQty; port++) {
    tmpRead = mapPot(adc.analogRead(port));
    while (tmpRead <= potsPrevVal[port] - 2 | tmpRead >= potsPrevVal[port] + 2) {
      controlChange(midiChannel, potsMidiController[port], tmpRead);
      // Serial.print("Pot # ");
      // Serial.print(port);
      // Serial.print(" value ");
      // Serial.println(tmpRead);
      potsPrevVal[port] = tmpRead;
      tmpRead = mapPot(adc.analogRead(port));
    }
  }

  //midiPresetReturn();
}
